// Logisim project Vezba.circ as structural Verilog: 1 circuit, main circuit main
module main (
  input  in_1,
  input  in_2,
  input  in_3,
  input  in_4,
  output out_5
);

  wire and_1_out, nand_1_out, nor_1_out, not_1_out, or_1_out, or_2_out, xor_2_out;
  wire [1:0] not_3_out, xor_3_out;
  wire [1:1] undriven;
  wire [4:0] not_2_out, not_4_out, xor_1_out;

  not not_1 (not_1_out, in_1);
  not not_2 (not_2_out[0], in_3);
  not not_3 (not_3_out[0], in_2);
  not not_4 (not_4_out[0], in_4);
  assign xor_1_out = not_4_out ^ not_2_out;  // XOR_Gate xor_1, 5 bits wide
  xor xor_2 (xor_2_out, in_2, not_1_out);
  nand nand_1 (nand_1_out, in_2, in_1);
  assign xor_3_out = not_3_out ^ {undriven[1], in_1};  // XOR_Gate xor_3, 2 bits wide
  and and_1 (and_1_out, xor_1_out[0], not_3_out[0]);
  or or_1 (or_1_out, in_3, nand_1_out);
  nor nor_1 (nor_1_out, and_1_out, xor_2_out);
  or or_2 (or_2_out, or_1_out, xor_3_out[0]);
  or or_3 (out_5, nor_1_out, or_2_out);
  // Pins of 1 and 2 bits meet at {undriven[1], in_1}
  // Pins of 1 and 5 bits meet at xor_1_out
  // Pins of 1 and 2 bits meet at not_3_out
  // Pins of 1 and 5 bits meet at not_4_out
  // Pins of 1 and 5 bits meet at not_2_out
  // Pins of 1 and 2 bits meet at xor_3_out
endmodule
